# Fritzing sketch scheme (saved by Fritzing 0.9.3b)
breadboards: 2

parts:
  Arduino = Arduino Leonardo (Rev3b)
  LED12 = LED - 5mm [color="Red (633nm)" package="5 mm [THT]"]
  LED13 = LED - 5mm [color="Red (633nm)" package="5 mm [THT]"]
  LED14 = LED - 5mm [color="Red (633nm)" package="5 mm [THT]"]
  LED15 = LED - 5mm [color="Red (633nm)" package="5 mm [THT]"]
  LED16 = LED - 5mm [color="Red (633nm)" package="5 mm [THT]"]
  S5 = Pushbutton [package=THT]
  S6 = Pushbutton [package=THT]
  S7 = Pushbutton [package=THT]
  S4 = Pushbutton [package=THT]
  J1 = Piezo Speaker
  part = Rotary Potentiometer (Small) [maximum_resistance=100kΩ package=THT]
  part_2 = Rotary Potentiometer (Small) [maximum_resistance=100kΩ package=THT]
  S8 = Toggle Switch [package=THT]
  S9 = Toggle Switch [package=THT]
  S10 = Toggle Switch [package=THT]
  part_3 = Resistor [tolerance=±5% resistance=220 package=THT]
  part_4 = Resistor [tolerance=±5% resistance=220 package=THT]
  part_5 = Resistor [tolerance=±5% resistance=220 package=THT]
  part_6 = Resistor [tolerance=±5% resistance=220 package=THT]
  part_7 = Resistor [tolerance=±5% resistance=220 package=THT]
  part_8 = Resistor [tolerance=±5% resistance=220 package=THT]
  D1 = Rectifier Diode [part_number=1N4001 package="300 mil [THT]"]
  LED17 = LED - 5mm [color="Red (633nm)" package="5 mm [THT]"]
  part_9 = Battery block 9V
  part_10 = Resistor [tolerance=±5% resistance=220 package=THT]
  part_11 = Resistor [tolerance=±5% resistance=220 package=THT]
  part_12 = Resistor [tolerance=±5% resistance=220 package=THT]
  LED11 = RGB LED (com. cathode, rbg) [package="5 mm [THT]"]

nets:
  N1: Arduino.D0/RX, S4.leg0
  N2: Arduino.D1/TX, S5.leg0
  N3: Arduino.D2/SDA, S6.leg0
  N4: Arduino.D3_PWM/SCL, part_7.Pin_1
  N5: Arduino.D4/A6, S7.leg0
  N6: Arduino.D5_PWM, part_6.Pin_1
  N7: Arduino.D6_PWM/A7, part_5.Pin_1
  N8: Arduino.D7, part_4.Pin_1
  N9: Arduino.5V, part.leg1, part_2.leg1
  N10: Arduino.GND, LED12.cathode, LED13.cathode, LED14.cathode, LED15.cathode, LED16.cathode, S5.leg1, S6.leg1, S7.leg1, S4.leg1, J1.pin1, part.leg2, part_2.leg2, S8.COM, S9.COM, S10.COM, LED17.cathode, part_9.-, LED11.common_cathode
  N11: Arduino.VIN, D1.cathode
  N12: Arduino.A0, part.wiper
  N13: Arduino.A1, part_2.wiper
  N14: Arduino.A2, S8.L1
  N15: Arduino.A3, S9.L1
  N16: Arduino.A4, S10.L1
  N17: Arduino.D8/A8, J1.pin2
  N18: Arduino.D9_PWM/A9, part_12.Pin_1
  N19: Arduino.D10_PWM/A10, part_11.Pin_1
  N20: Arduino.D11_PWM, part_8.Pin_1
  N21: Arduino.D12/A11, part_3.Pin_1
  N22: Arduino.D13_PWM, part_10.Pin_1
  N23: LED12.anode, part_4.Pin_0
  N24: LED13.anode, part_8.Pin_0
  N25: LED14.anode, part_3.Pin_0
  N26: LED15.anode, part_5.Pin_0
  N27: LED16.anode, part_6.Pin_0
  N28: part_7.Pin_0, LED17.anode
  N29: D1.anode, part_9.+
  N30: part_10.Pin_0, LED11.green_anode
  N31: part_11.Pin_0, LED11.blue_anode
  N32: part_12.Pin_0, LED11.red_anode
